# Fritzing sketch MCE 202 project (saved by Fritzing 0.8.7b)
breadboards: 1

parts:
  Eleman1 = RFID USB Reader  # not connected
  Eleman2 = Arduino Uno (Rev3)
  LED1 = LED - 5mm [color="Red (633nm)" package="5 mm [THT]"]
  LED2 = RGB LED (com. cathode, rgb) [package="5 mm [THT]"]
  J1 = Basic Servo
  J2 = Piezo Speaker

nets:
  N1: Eleman2.D3_PWM, LED2.green_anode
  N2: Eleman2.D4, LED1.anode
  N3: Eleman2.D6_PWM, J2.pin2
  N4: Eleman2.D7, J1.pulse
  3V3: Eleman2.3V3, J1.vcc
  N5: Eleman2.GND, LED1.cathode, LED2.common_cathode, J2.pin1
